// Logisim project UNRN-ED-ALU-backup (1).circ as structural Verilog
module SumCompleto_1bit (
  input  A,
  input  B,
  input  Cin,
  output S,
  output Cout
);

  wire and_1_out, and_2_out, xor_1_out;

  xor xor_1 (xor_1_out, A, B);
  xor xor_2 (S, xor_1_out, Cin);
  and and_1 (and_1_out, xor_1_out, Cin);
  and and_2 (and_2_out, B, A);
  or or_1 (Cout, and_1_out, and_2_out);

  // Notes on the sheet:
  //   Sumador completo de 1 Bit
  //   Nro de Grupo: 28
endmodule

module SumCompleto_4bits (
  input  [3:0] A,
  input  [3:0] B,
  input  Cin,
  output [3:0] S,
  output Cout
);

  wire sumcompleto_1bit_1_cout, sumcompleto_1bit_2_cout, sumcompleto_1bit_3_cout;

  SumCompleto_1bit sumcompleto_1bit_1 (.A(A[0]), .B(B[0]), .Cin(Cin), .S(S[0]), .Cout(sumcompleto_1bit_1_cout));
  SumCompleto_1bit sumcompleto_1bit_2 (
    .A(A[1]), .B(B[1]), .Cin(sumcompleto_1bit_1_cout), .S(S[1]), .Cout(sumcompleto_1bit_2_cout));
  SumCompleto_1bit sumcompleto_1bit_3 (
    .A(A[2]), .B(B[2]), .Cin(sumcompleto_1bit_2_cout), .S(S[2]), .Cout(sumcompleto_1bit_3_cout));
  SumCompleto_1bit sumcompleto_1bit_4 (.A(A[3]), .B(B[3]), .Cin(sumcompleto_1bit_3_cout), .S(S[3]), .Cout(Cout));

  // Notes on the sheet:
  //   Sumador completo de 4 Bits
  //   Nro de Grupo: 28
endmodule

module Flag_Cero (
  input  [3:0] S,
  output Z
);

  nor nor_1 (Z, S[0], S[1], S[2], S[3]);

  // Notes on the sheet:
  //   Flag - Cero (Z)
  //   Nro de Grupo: 28
endmodule

module Flag_Overflow (
  input  a3,
  input  b3,
  input  s3,
  output V
);

  wire xnor_1_out, xor_1_out;

  xnor xnor_1 (xnor_1_out, b3, a3);
  xor xor_1 (xor_1_out, s3, a3);
  and and_1 (V, xnor_1_out, xor_1_out);

  // Notes on the sheet:
  //   Flag - Overflow (V)
  //   Nro de Grupo: 28
endmodule

module ComplementadorA2 (
  input  [3:0] B,
  input  Neg,
  output [3:0] B_star
);

  wire [3:0] not_1_out, sumcompleto_4bits_1_s;

  assign not_1_out = ~B;  // NOT_Gate not_1, 4 bits wide
  SumCompleto_4bits sumcompleto_4bits_1 (
    .S(sumcompleto_4bits_1_s), .A(not_1_out), .B(4'b0001), .Cin(1'b0));  // open: Cout
  Hex_Digit_Display hex_digit_display_1 (.value(B_star));  // open: dp
  Multiplexer #(.width(4)) multiplexer_1 (.in0(B), .in1(sumcompleto_4bits_1_s), .out(B_star), .sel(Neg));  // open: en

  // Notes on the sheet:
  //   Complementador a 2
  //   Nro de Grupo: 28
  //   Neg  ALU
  //   0    B
  //   1   -B
endmodule

module UnidadAritmetica (
  input  [3:0] A,
  input  [3:0] B,
  input  OP,
  output V,
  output N,
  output Z,
  output C,
  output [3:0] S
);

  wire not_1_out, sumcompleto_4bits_1_cout;
  wire [3:0] complementadora2_1_b_star;

  ComplementadorA2 complementadora2_1 (.B_star(complementadora2_1_b_star), .B(B), .Neg(OP));
  not not_1 (not_1_out, sumcompleto_4bits_1_cout);
  SumCompleto_4bits sumcompleto_4bits_1 (
    .S({N, S[2:0]}), .Cout(sumcompleto_4bits_1_cout), .A(A), .B(complementadora2_1_b_star), .Cin(1'b0));
  Flag_Overflow flag_overflow_1 (.V(V), .a3(A[3]), .b3(complementadora2_1_b_star[3]), .s3(N));
  Multiplexer multiplexer_1 (.in0(sumcompleto_4bits_1_cout), .in1(not_1_out), .out(C), .sel(OP));  // open: en
  Flag_Cero flag_cero_1 (.Z(Z), .S({N, S[2:0]}));
  Hex_Digit_Display hex_digit_display_1 (.value({N, S[2:0]}));  // open: dp
  SumCompleto_4bits sumcompleto_4bits_2 ();  // open: S, Cout, A, B, Cin

  assign S[3] = N;

  // Notes on the sheet:
  //   Unidad Aritmetica (Suma/Resta)
  //   Nro de Grupo: 28
  //   OP   ALU
  //   0  A + B
  //   1  A - B
endmodule

module ALU (
  input  [3:0] A,
  input  [3:0] B,
  input  [1:0] OP,
  output V,
  output N,
  output Z,
  output C,
  output [3:0] S
);

  wire [3:0] and_1_out, or_1_out, unidadaritmetica_1_s;

  UnidadAritmetica unidadaritmetica_1 (.OP(OP[0]), .V(V), .N(N), .Z(Z), .C(C), .S(unidadaritmetica_1_s), .A(A), .B(B));
  assign and_1_out = B & A;  // AND_Gate and_1, 4 bits wide
  assign or_1_out = B | A;  // OR_Gate or_1, 4 bits wide
  Multiplexer #(.select(2), .width(4)) multiplexer_1 (
    .in0(unidadaritmetica_1_s), .in1(unidadaritmetica_1_s), .in2(and_1_out), .in3(or_1_out), .out(S), .sel(OP));  // open: en
  Hex_Digit_Display hex_digit_display_1 (.value(S));  // open: dp

  // Notes on the sheet:
  //   ALU (Suma/Resta/AND/OR)
  //   Nro de Grupo: 28
  //   OP   ALU
  //   0 0  A + B
  //   0 1  A - B
  //   1 0  A and B
  //   1 1  A or  B
endmodule

module SumCompleto_8bits (
  input  Cin,
  input  [7:0] A,
  input  [7:0] B,
  output [7:0] S,
  output Cout
);

  wire sumcompleto_1bit_1_cout, sumcompleto_1bit_2_cout, sumcompleto_1bit_3_cout, sumcompleto_1bit_4_cout,
       sumcompleto_1bit_5_cout, sumcompleto_1bit_6_cout, sumcompleto_1bit_7_cout;

  SumCompleto_1bit sumcompleto_1bit_1 (.A(A[0]), .B(B[0]), .Cin(Cin), .S(S[0]), .Cout(sumcompleto_1bit_1_cout));
  SumCompleto_1bit sumcompleto_1bit_2 (
    .A(A[1]), .B(B[1]), .Cin(sumcompleto_1bit_1_cout), .S(S[1]), .Cout(sumcompleto_1bit_2_cout));
  SumCompleto_1bit sumcompleto_1bit_3 (
    .A(B[2]), .B(A[2]), .Cin(sumcompleto_1bit_2_cout), .S(S[2]), .Cout(sumcompleto_1bit_3_cout));
  SumCompleto_1bit sumcompleto_1bit_4 (
    .A(A[3]), .B(B[3]), .Cin(sumcompleto_1bit_3_cout), .S(S[3]), .Cout(sumcompleto_1bit_4_cout));
  SumCompleto_1bit sumcompleto_1bit_5 (
    .A(A[4]), .B(B[4]), .Cin(sumcompleto_1bit_4_cout), .S(S[4]), .Cout(sumcompleto_1bit_5_cout));
  SumCompleto_1bit sumcompleto_1bit_6 (
    .A(A[5]), .B(B[5]), .Cin(sumcompleto_1bit_5_cout), .S(S[5]), .Cout(sumcompleto_1bit_6_cout));
  SumCompleto_1bit sumcompleto_1bit_7 (
    .A(A[6]), .B(B[6]), .Cin(sumcompleto_1bit_6_cout), .S(S[6]), .Cout(sumcompleto_1bit_7_cout));
  SumCompleto_1bit sumcompleto_1bit_8 (.A(A[7]), .B(B[7]), .Cin(sumcompleto_1bit_7_cout), .S(S[7]), .Cout(Cout));
endmodule
